// Logisim project projet1.circ as structural Verilog: 2 circuits, main circuit main
module main (
  input  [7:0] nb1,
  input  [7:0] nb2,
  input  [1:0] \Opération ,
  input  Enable
);

  wire calculateur_1_depassement;
  wire [7:0] \calculateur_1_résultat ;

  LED led_1 (.in(calculateur_1_depassement));
  calculateur calculateur_1 (
    .nb1(nb1), .nb2(nb2), .Operation(\Opération ), .in_4(Enable), .Depassement(calculateur_1_depassement),
    .\Résultat (\calculateur_1_résultat ));
  // Probe on \calculateur_1_résultat 
endmodule

module calculateur (
  input  [7:0] nb1,
  input  [7:0] nb2,
  input  [1:0] Operation,
  input  in_4,
  output Depassement,
  output [7:0] \Résultat 
);

  wire adder_1_cout, comparator_1_eq, comparator_1_gt, comparator_1_lt, or_1_out, subtractor_1_bout;
  wire [7:0] adder_1_out, controlled_buffer_1_out, controlled_buffer_2_out, divider_1_out, divider_2_out,
       multiplexer_1_out, multiplexer_2_out, multiplier_1_out, subtractor_1_out, subtractor_2_out;

  Adder adder_1 (.a(nb1), .b(nb2), .out(adder_1_out), .cout(adder_1_cout));  // open: cin
  Divider divider_1 (.a(nb1), .b(nb2), .out(divider_1_out));  // open: upper, rem
  Divider divider_2 (.a(nb2), .b(nb1), .out(divider_2_out));  // open: upper, rem
  Subtractor subtractor_1 (.a(nb1), .b(nb2), .out(subtractor_1_out), .bout(subtractor_1_bout));  // open: bin
  Subtractor subtractor_2 (.a(nb2), .b(nb1), .out(subtractor_2_out));  // open: bin, bout
  Multiplier multiplier_1 (.a(nb1), .b(nb2), .out(multiplier_1_out));  // open: cin, cout
  assign controlled_buffer_1_out = or_1_out ? divider_1_out : 8'bz;  // Controlled_Buffer controlled_buffer_1
  or or_1 (or_1_out, comparator_1_gt, comparator_1_eq, comparator_1_lt);
  Comparator comparator_1 (
    .a(divider_1_out), .b(divider_2_out), .gt(comparator_1_gt), .eq(comparator_1_eq), .lt(comparator_1_lt));
  assign controlled_buffer_2_out = comparator_1_lt ? divider_2_out : 8'bz;  // Controlled_Buffer controlled_buffer_2
  Multiplexer #(.width(8)) multiplexer_1 (
    .in0(subtractor_1_out), .in1(subtractor_2_out), .out(multiplexer_1_out), .sel(subtractor_1_bout),
    .en(in_4));
  Multiplexer #(.width(8)) multiplexer_2 (
    .in0(controlled_buffer_1_out), .in1(controlled_buffer_2_out), .out(multiplexer_2_out),
    .sel(comparator_1_lt), .en(in_4));
  Multiplexer #(.select(2)) multiplexer_3 (
    .in1(adder_1_cout), .out(Depassement), .sel(Operation), .en(in_4));  // open: in0, in2, in3
  Multiplexer #(.select(2), .width(8)) multiplexer_4 (
    .in0(adder_1_out), .in1(multiplexer_1_out), .in2(multiplier_1_out), .in3(multiplexer_2_out),
    .out(\Résultat ), .sel(Operation), .en(in_4));
endmodule
